// Logisim project RSC.circ as structural Verilog: 9 circuits, main circuit Arith_U
// AU
module Arith_U (
  input  [31:0] A,
  input  [31:0] B,
  input  S1,
  input  S0,
  output [31:0] AU_out
);

  wire and_1_out, xnor_1_out;
  wire [31:0] adder_1_out, multiplexer_1_out, not_1_out;

  assign not_1_out = ~B;  // NOT_Gate not_1, 32 bits wide
  Multiplexer #(.select(2), .width(32), .enable("false")) multiplexer_1 (
    .in0(not_1_out), .in1(B), .in2(32'h1), .out(multiplexer_1_out), .sel({S1, S0}));  // open: in3
  xnor xnor_1 (xnor_1_out, S1, S0);
  Adder #(.width(32)) adder_1 (.a(A), .b(multiplexer_1_out), .out(adder_1_out), .cin(xnor_1_out));  // open: cout
  Multiplexer #(.width(32), .enable("false")) multiplexer_2 (.in0(adder_1_out), .in1(B), .out(AU_out), .sel(and_1_out));
  and and_1 (and_1_out, S0, S1);

  // Notes on the sheet:
  //    Tien Dinh
  //   CLA4
  //   AU
endmodule

// LU
module Logic_U (
  input  [31:0] A,
  input  [31:0] B,
  input  S1,
  input  S0,
  output [31:0] Logic_Out
);

  wire [31:0] and_1_out, not_1_out, or_1_out, shifter_1_out;

  assign not_1_out = ~A;  // NOT_Gate not_1, 32 bits wide
  Shifter #(.width(32), .shift("ar")) shifter_1 (.in(A), .\dist (5'b00001), .out(shifter_1_out));
  assign and_1_out = A & B;  // AND_Gate and_1, 32 bits wide
  assign or_1_out = A | B;  // OR_Gate or_1, 32 bits wide
  Multiplexer #(.select(2), .width(32), .enable("false")) multiplexer_1 (
    .in0(and_1_out), .in1(or_1_out), .in2(shifter_1_out), .in3(not_1_out), .out(Logic_Out), .sel({S1, S0}));

  // Notes on the sheet:
  //   Tien Dinh
  //   CLA6
  //   LU
endmodule

module ALU (
  input  [31:0] A,
  input  [31:0] B,
  input  S2,
  input  S1,
  input  S0,
  output [31:0] ALU_Out
);

  wire [31:0] arith_u_1_au_out, logic_u_1_logic_out;

  Arith_U arith_u_1 (.A(A), .B(B), .S1(S1), .S0(S0), .AU_out(arith_u_1_au_out));
  Logic_U logic_u_1 (.A(A), .B(B), .S1(S1), .S0(S0), .Logic_Out(logic_u_1_logic_out));
  Multiplexer #(.width(32)) multiplexer_1 (
    .in0(arith_u_1_au_out), .in1(logic_u_1_logic_out), .out(ALU_Out), .sel(S2));  // open: en

  // Notes on the sheet:
  //   Tien Dinh
  //   CLA6
  //   ALU
endmodule

module SC (
  input  Clock,
  input  Clear,
  output [2:0] SEQ_out
);

  wire [2:0] adder_1_out;

  Adder #(.width(3)) adder_1 (.a(SEQ_out), .b(3'b001), .out(adder_1_out));  // open: cin, cout
  Register #(.width(3)) register_1 (.D(adder_1_out), .Q(SEQ_out), .clk(Clock), .clr(Clear));  // open: en

  // Notes on the sheet:
  //   Tien Dinh
  //   CLA 7
  //   SC
endmodule

module RSC (
  output [7:0] Timer,
  output [3:0] Decoder
);

  wire control_1_acc_bus, control_1_acc_clr, control_1_acc_ld, control_1_ar_ld, control_1_dr_bus,
       control_1_dr_ld, control_1_ir_ld, control_1_outr_ld, control_1_pc_bus, control_1_pc_inc,
       control_1_pc_ld, control_1_r_bus, control_1_r_ld, control_1_ram_en, control_1_ram_r_prime_w,
       control_1_z_ld, Primary_Clock_out, z_reg_1_z_out;
  wire [2:0] control_1_alu_s;
  wire [31:0] acc_1_data_out, alu_1_alu_out, ar_1_data_out, dr_1_data_out, ir_1_data_out, outr_1_data_out,
       r_1_bus_out;

  Clock Primary_Clock (.out(Primary_Clock_out));
  AR ar_1 (.Data_In(r_1_bus_out), .Clock(Primary_Clock_out), .Load(control_1_ar_ld), .Data_Out(ar_1_data_out));
  R r_1 (
    .Data_In(r_1_bus_out), .Clock(Primary_Clock_out), .Load(control_1_r_ld), .Bus(control_1_r_bus),
    .Bus_Out(r_1_bus_out));  // open: Data_Out
  ALU alu_1 (
    .A(acc_1_data_out), .B(r_1_bus_out), .S2(control_1_alu_s[2]), .S1(control_1_alu_s[1]),
    .S0(control_1_alu_s[0]), .ALU_Out(alu_1_alu_out));
  DR dr_1 (
    .Data_In(r_1_bus_out), .Clock(Primary_Clock_out), .Load(control_1_dr_ld), .Bus(control_1_dr_bus),
    .Data_Out(dr_1_data_out), .Bus_Out(r_1_bus_out));
  PC pc_1 (
    .Data_In(r_1_bus_out), .Clock(Primary_Clock_out), .Load(control_1_pc_ld), .Count(control_1_pc_inc),
    .Bus(control_1_pc_bus), .Bus_Out(r_1_bus_out));  // open: Data_Out
  ACC acc_1 (
    .Data_In(alu_1_alu_out), .Clock(Primary_Clock_out), .Load(control_1_acc_ld), .Clear(control_1_acc_clr),
    .Bus(control_1_acc_bus), .Data_Out(acc_1_data_out), .Bus_Out(r_1_bus_out));
  RAM #(.addrWidth(16), .dataWidth(32)) ram_1 (
    .addr(ar_1_data_out[15:0]), .data(r_1_bus_out), .sel(control_1_ram_en), .clk(Primary_Clock_out),
    .ld(control_1_ram_r_prime_w));  // open: clr
  OUTR outr_1 (.Data_In(r_1_bus_out), .Clock(Primary_Clock_out), .Load(control_1_outr_ld), .Data_Out(outr_1_data_out));
  Z_Reg z_reg_1 (.ACC_in(acc_1_data_out), .Clock(Primary_Clock_out), .Load(control_1_z_ld), .Z_out(z_reg_1_z_out));
  IR ir_1 (.Data_In(dr_1_data_out), .Clock(Primary_Clock_out), .Load(control_1_ir_ld), .Data_Out(ir_1_data_out));
  Control control_1 (
    .RAM_R_prime_W(control_1_ram_r_prime_w), .RAM_EN(control_1_ram_en), .AR_LD(control_1_ar_ld),
    .PC_BUS(control_1_pc_bus), .PC_INC(control_1_pc_inc), .PC_LD(control_1_pc_ld), .DR_BUS(control_1_dr_bus),
    .DR_LD(control_1_dr_ld), .R_BUS(control_1_r_bus), .R_LD(control_1_r_ld), .ACC_BUS(control_1_acc_bus),
    .ACC_CLR(control_1_acc_clr), .ACC_LD(control_1_acc_ld), .ALU_S(control_1_alu_s),
    .OUTR_LD(control_1_outr_ld), .Z_LD(control_1_z_ld), .IR_LD(control_1_ir_ld), .Clock(Primary_Clock_out),
    .Z_In(z_reg_1_z_out), .T(Timer), .IR_In(ir_1_data_out), .D(Decoder));
  Hex_Digit_Display hex_digit_display_1 (.value(outr_1_data_out[27:24]));  // open: dp
  Hex_Digit_Display hex_digit_display_2 (.value(outr_1_data_out[31:28]));  // open: dp
  Hex_Digit_Display hex_digit_display_3 (.value(outr_1_data_out[23:20]));  // open: dp
  Hex_Digit_Display hex_digit_display_4 (.value(outr_1_data_out[19:16]));  // open: dp
  Hex_Digit_Display hex_digit_display_5 (.value(outr_1_data_out[15:12]));  // open: dp
  Hex_Digit_Display hex_digit_display_6 (.value(outr_1_data_out[7:4]));  // open: dp
  Hex_Digit_Display hex_digit_display_7 (.value(outr_1_data_out[11:8]));  // open: dp
  Hex_Digit_Display hex_digit_display_8 (.value(outr_1_data_out[3:0]));  // open: dp

  // Notes on the sheet:
  //   Tien Dinh
  //   OLA6
  //   Bus loop and Memory
endmodule

// Decoder
module Decorder (
  input  [31:0] IR_In,
  output [15:0] D_Out,
  output [3:0] Instruction
);

  wire or_2_out;
  wire [3:0] or_1_out;
  wire [15:0] decoder_1_out0;

  Multiplexer #(.width(16), .enable("false")) multiplexer_1 (
    .in0(decoder_1_out0), .in1({16{1'b0}}), .out(D_Out), .sel(or_2_out));
  Decoder #(.select(4), .enable("false")) decoder_1 (
    .out0(decoder_1_out0[0]), .out1(decoder_1_out0[1]), .out2(decoder_1_out0[2]), .out3(decoder_1_out0[3]),
    .out4(decoder_1_out0[4]), .out5(decoder_1_out0[5]), .out6(decoder_1_out0[6]), .out7(decoder_1_out0[7]),
    .out8(decoder_1_out0[8]), .out9(decoder_1_out0[9]), .out10(decoder_1_out0[10]),
    .out11(decoder_1_out0[11]), .out12(decoder_1_out0[12]), .out13(decoder_1_out0[13]),
    .out14(decoder_1_out0[14]), .out15(decoder_1_out0[15]), .sel(IR_In[3:0]));
  assign or_1_out = IR_In[7:4] | IR_In[11:8] | IR_In[15:12] | IR_In[19:16] | IR_In[23:20] | IR_In[27:24] | IR_In[31:28];  // OR_Gate or_1, 4 bits wide
  or or_2 (or_2_out, or_1_out[3], or_1_out[2], or_1_out[1], or_1_out[0]);

  assign Instruction = IR_In[3:0];

  // Notes on the sheet:
  //   Tien Dinh
  //   CLA8
  //   Decoder
endmodule

module Timer (
  input  Clock,
  input  Stop,
  input  Clear,
  output [7:0] T_Out
);

  wire [2:0] sc_1_seq_out;
  wire [7:0] decoder_1_out0;

  Multiplexer #(.width(8)) multiplexer_1 (.in0(decoder_1_out0), .in1({8{1'b0}}), .out(T_Out), .sel(Stop));  // open: en
  Decoder #(.select(3), .enable("false")) decoder_1 (
    .out0(decoder_1_out0[0]), .out1(decoder_1_out0[1]), .out2(decoder_1_out0[2]), .out3(decoder_1_out0[3]),
    .out4(decoder_1_out0[4]), .out5(decoder_1_out0[5]), .out6(decoder_1_out0[6]), .out7(decoder_1_out0[7]),
    .sel(sc_1_seq_out));
  SC sc_1 (.Clock(Clock), .Clear(Clear), .SEQ_out(sc_1_seq_out));

  // Notes on the sheet:
  //   Tien Dinh
  //   CLA8
  //   Timer
endmodule

// Z
module Z_Reg (
  input  Clock,
  input  [31:0] ACC_in,
  input  Load,
  output Z_out
);

  wire nor_1_out;

  nor nor_1 (nor_1_out, ACC_in[0], ACC_in[1], ACC_in[2], ACC_in[3], ACC_in[4], ACC_in[5], ACC_in[6], ACC_in[7], ACC_in[8], ACC_in[9], ACC_in[10], ACC_in[11], ACC_in[12], ACC_in[13], ACC_in[14], ACC_in[15], ACC_in[16], ACC_in[17], ACC_in[18], ACC_in[19], ACC_in[20], ACC_in[21], ACC_in[22], ACC_in[23], ACC_in[24], ACC_in[25], ACC_in[26], ACC_in[27], ACC_in[28], ACC_in[29], ACC_in[30], ACC_in[31]);
  _1bit_reg u_1bit_reg_1 (.Data(nor_1_out), .Clock(Clock), .Load(Load), .Data_out(Z_out));  // open: Clear

  // Notes on the sheet:
  //   Tien Dinh
  //   Z_Reg
endmodule

module Control (
  input  Clock,
  input  [31:0] IR_In,
  input  Z_In,
  output IR_LD,
  output [7:0] T,
  output RAM_R_prime_W,
  output [3:0] D,
  output RAM_EN,
  output AR_LD,
  output PC_BUS,
  output PC_INC,
  output PC_LD,
  output DR_BUS,
  output DR_LD,
  output R_BUS,
  output R_LD,
  output ACC_BUS,
  output ACC_CLR,
  output ACC_LD,
  output [2:0] ALU_S,
  output OUTR_LD,
  output Z_LD
);

  wire and_1_out, S_data_out;
  wire [15:0] decorder_1_d_out;

  RAM_RW ram_rw_1 (
    .t1(T[1]), .t3(T[3]), .t5(T[5]), .d1(decorder_1_d_out[1]), .d2(decorder_1_d_out[2]),
    .d5(decorder_1_d_out[5]), .d6(decorder_1_d_out[6]), .z(Z_In), .RAM_RW(RAM_R_prime_W));
  RAM_EN ram_en_1 (
    .t1(T[1]), .t3(T[3]), .t5(T[5]), .t6(T[6]), .d1(decorder_1_d_out[1]), .d2(decorder_1_d_out[2]),
    .d5(decorder_1_d_out[5]), .d6(decorder_1_d_out[6]), .z(Z_In), .RAM_EN(RAM_EN));
  AR_LD ar_ld_1 (
    .t0(T[0]), .t2(T[2]), .t4(T[4]), .clock(Clock), .d1(decorder_1_d_out[1]), .d2(decorder_1_d_out[2]),
    .AR_LD(AR_LD));
  PC_BUS pc_bus_1 (.t0(T[0]), .t2(T[2]), .PC_BUS(PC_BUS));
  PC_INC pc_inc_1 (
    .t1(T[1]), .t3(T[3]), .clock(Clock), .d1(decorder_1_d_out[1]), .d2(decorder_1_d_out[2]),
    .d6(decorder_1_d_out[6]), .z(Z_In), .PC_INC(PC_INC));
  PC_LD pc_ld_1 (.t4(T[4]), .clock(Clock), .d5(decorder_1_d_out[5]), .d6(decorder_1_d_out[6]), .z(Z_In), .PC_LD(PC_LD));
  DR_BUS dr_bus_1 (
    .t4(T[4]), .t6(T[6]), .d1(decorder_1_d_out[1]), .d2(decorder_1_d_out[2]), .d5(decorder_1_d_out[5]),
    .d6(decorder_1_d_out[6]), .z(Z_In), .DR_BUS(DR_BUS));
  DR_LD dr_ld_1 (
    .t1(T[1]), .t3(T[3]), .t5(T[5]), .clock(Clock), .d1(decorder_1_d_out[1]), .d2(decorder_1_d_out[2]),
    .d5(decorder_1_d_out[5]), .d6(decorder_1_d_out[6]), .z(Z_In), .DR_LD(DR_LD));
  R_BUS r_bus_1 (
    .t3(T[3]), .d4(decorder_1_d_out[4]), .d8(decorder_1_d_out[8]), .d9(decorder_1_d_out[9]),
    .d12(decorder_1_d_out[12]), .d13(decorder_1_d_out[13]), .R_BUS(R_BUS));
  R_LD r_ld_1 (.t3(T[3]), .clock(Clock), .d3(decorder_1_d_out[3]), .R_LD(R_LD));
  ACC_BUS acc_bus_1 (
    .t3(T[3]), .t5(T[5]), .d2(decorder_1_d_out[2]), .d3(decorder_1_d_out[3]), .d7(decorder_1_d_out[7]),
    .ACC_BUS(ACC_BUS));
  ACC_CLR acc_clr_1 (.t3(T[3]), .d11(decorder_1_d_out[11]), .ACC_CLR(ACC_CLR));
  ACC_LD acc_ld_1 (
    .t3(T[3]), .t6(T[6]), .clock(Clock), .d1(decorder_1_d_out[1]), .d4(decorder_1_d_out[4]),
    .d8(decorder_1_d_out[8]), .d9(decorder_1_d_out[9]), .d10(decorder_1_d_out[10]),
    .d12(decorder_1_d_out[12]), .d13(decorder_1_d_out[13]), .d14(decorder_1_d_out[14]),
    .d15(decorder_1_d_out[15]), .ACC_LD(ACC_LD));
  ALU_SEL_s2 alu_sel_s2_1 (
    .d1(decorder_1_d_out[1]), .d4(decorder_1_d_out[4]), .d9(decorder_1_d_out[9]), .d10(decorder_1_d_out[10]),
    .d12(decorder_1_d_out[12]), .d13(decorder_1_d_out[13]), .d14(decorder_1_d_out[14]),
    .d15(decorder_1_d_out[15]), .s0(ALU_S[0]), .s1(ALU_S[1]), .s2(ALU_S[2]));
  OUTR_LD outr_ld_1 (.t3(T[3]), .clock(Clock), .d7(decorder_1_d_out[7]), .OUTR_LC(OUTR_LD));
  IR_LD ir_ld_1 (.t2(T[2]), .clock(Clock), .IR_LD(IR_LD));
  and and_1 (and_1_out, decorder_1_d_out[0], T[3]);
  Timer timer_1 (.T_Out(T), .Clock(Clock), .Stop(S_data_out));  // open: Clear
  Decorder decorder_1 (.D_Out(decorder_1_d_out), .Instruction(D), .IR_In(IR_In));
  _1bit_reg S (.Data(1'b1), .Clock(Clock), .Load(and_1_out), .Clear(1'b0), .Data_out(S_data_out));

  assign Z_LD = 1'b1;
endmodule
